# Fritzing sketch mini projet (3) (saved by Fritzing 0.9.3b)

parts:
  U1 = NodeMCU V3.0
  HC-SR04_Sensor_1 = HC-SR04 Ultrasonic Distance Sensor
  M1 = Getriebemotor
  L298N1 = L298N DC motor driver
  VCC1 = 4 x AA Battery Box
  J1 = Piezo Speaker
  GY1 = MPU-6050 Board GY-521 [form="♀ (female)" package=THT]

nets:
  N1: U1.D1, GY1.pin3
  N2: U1.D2, GY1.pin4
  N3: U1.D3, L298N1.IN3
  N4: U1.D4, L298N1.IN4
  N5: U1.3V3, GY1.pin1
  GND: U1.GND, HC-SR04_Sensor_1.GND, L298N1.GND, VCC1.-, GY1.pin2
  N6: U1.D5, HC-SR04_Sensor_1.ECHO
  N7: U1.D6, HC-SR04_Sensor_1.TRIG
  N8: U1.D7, L298N1.ENB
  N9: U1.D8, J1.pin2
  VIN: U1.Vin, HC-SR04_Sensor_1.VCC
  N10: M1.pin_1, L298N1.OUT4
  N11: M1.pin_2, L298N1.OUT3

custom parts:
  NodeMCU V3.0: NodeMcu V3 Lua WIFI Development Board
  L298N DC motor driver: 2x DC motor driver with 78M05 positive voltage regulator (7..35 V) L298N: max 46 V, 2 A Set 5 V Enable jumper to enable 5 V regultor (needed for the L298N) and +5 V output at screw terminal or supply external +5 V at screw terminal Set ENA and/or ENB to +5 V to enable motor permanently or supply ENA and/or ENB with PWM signal IN1 and IN2 set rotation directory for motor A (OUT1/OUT2) IN2 and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
  4 x AA Battery Box: A 4 x AA battery box.
  MPU-6050 Board GY-521: Acelerometro y Giroscopio MPU-6050 Board GY-521
